# Fritzing sketch midi3v3 (saved by Fritzing 0.7.11b)
breadboards: 1

parts:
  R1 = Resistor [resistance=47 tolerance=±5% package=THT]
  IC1 = IC, DIP package, 8 pins [chip_label=6N138 spacing=300mil]
  R2 = Resistor [resistance=220 tolerance=±5% package=THT]
  D1 = Rectifier Diode [part_number=1N4001 package="300 mil [THT]"]
  R3 = Resistor [resistance=220 tolerance=±5% package=THT]
  Q1 = PNP-Transistor [package="TO92 [THT]"]
  R4 = Resistor [resistance=10k tolerance=±5% package=THT]
  R5 = Resistor [resistance=47 tolerance=±5% package=THT]
  J3 = female pin header, 3 pins [form="♀ (female)"]
  J4 = female pin header, 2 pins [form="♀ (female)"]
  J2 = female pin header, 4 pins [form="♀ (female)"]
  DIN1 = DIN-5 jack (MIDI) [package=THT]
  DIN2 = DIN-5 jack (MIDI) [package=THT]

nets:
  N1: R1.Pin_0, DIN1.5
  N2: R1.Pin_1, IC1.pin8, R2.Pin_0, R4.Pin_0, J3.pin2, J2.pin1
  N3: IC1.pin2, D1.cathode, R3.Pin_0
  N4: IC1.pin3, D1.anode, DIN2.4
  N5: IC1.pin5, Q1.C, J3.pin1, J4.pin2, J2.pin2, DIN1.2, DIN1.GND
  N6: IC1.pin6, R2.Pin_1, J2.pin4
  N7: R3.Pin_1, DIN2.5
  N8: Q1.E, R4.Pin_1, R5.Pin_1
  N9: Q1.B, J2.pin3
  N10: R5.Pin_0, DIN1.4
  N11: J3.pin3, J4.pin1
